# Fritzing sketch pong (saved by Fritzing 0.9.10b)
breadboards: 3

parts:
  M1 = ESP32-S3-DevKitC-1 [part_number=ESP32-S3-DevKitC-1]
  D1 = LED_BARGRAPH_10 [package=led_bargaph_10]
  R1 = Resistor [tolerance=±5% resistance=330 package="0603 [SMD]"]
  R2 = Resistor [tolerance=±5% resistance=330 package="0603 [SMD]"]
  R3 = Resistor [tolerance=±5% resistance=330 package="0603 [SMD]"]
  R4 = Resistor [tolerance=±5% resistance=330 package="0603 [SMD]"]
  R5 = Resistor [tolerance=±5% resistance=330 package="0603 [SMD]"]
  R6 = Resistor [tolerance=±5% resistance=330 package="0603 [SMD]"]
  R7 = Resistor [tolerance=±5% resistance=330 package="0603 [SMD]"]
  R8 = Resistor [tolerance=±5% resistance=330 package="0603 [SMD]"]
  R9 = Resistor [tolerance=±5% resistance=330 package="0603 [SMD]"]
  R10 = Resistor [tolerance=±5% resistance=330 package="0603 [SMD]"]
  LED1 = smd LED [color="Blue (430nm)" package="0805 [SMD]"]
  LED2 = smd LED [color="Green (555nm)" package="0805 [SMD]"]
  LED3 = smd LED [color="Yellow (585nm)" package="0805 [SMD]"]
  LED4 = smd LED [color="Orange (620nm)" package="0805 [SMD]"]
  LED5 = smd LED [color="Red (633nm)" package="0805 [SMD]"]
  R11 = Resistor [tolerance=±5% resistance=330 package="0603 [SMD]"]
  R12 = Resistor [tolerance=±5% resistance=330 package="0603 [SMD]"]
  R13 = Resistor [tolerance=±5% resistance=330 package="0603 [SMD]"]
  R14 = Resistor [tolerance=±5% resistance=330 package="0603 [SMD]"]
  R15 = Resistor [tolerance=±5% resistance=330 package="0603 [SMD]"]
  LED6 = smd LED [color="Green (555nm)" package="0805 [SMD]"]
  R16 = Resistor [tolerance=±5% resistance=330 package="0603 [SMD]"]
  S1 = Pushbutton [package="[SMD]"]
  R17 = Resistor [tolerance=±5% resistance=330 package="0603 [SMD]"]

nets:
  N1: M1.pin_1, M1.pin_2, S1.Pin_3, S1.Pin_4
  N2: M1.pin_4, D1.A_C
  N3: M1.pin_5, D1.B_C
  N4: M1.pin_6, D1.C_C
  N5: M1.pin_7, D1.D_C
  N6: M1.pin_8, D1.E_C
  N7: M1.pin_9, D1.F_C
  N8: M1.pin_10, D1.G_C
  N9: M1.pin_11, D1.H_C
  N10: M1.pin_12, D1.I_C
  N11: M1.pin_13, D1.J_C
  N12: M1.pin_14, S1.Pin_1, S1.Pin_2, R17.Pin_1
  N13: M1.pin_15, LED6.anode
  N14: M1.pin_16, LED5.anode
  N15: M1.pin_17, LED4.anode
  N16: M1.pin_18, LED3.anode
  N17: M1.pin_19, LED2.anode
  N18: M1.pin_20, LED1.anode
  N19: M1.pin_22, M1.pin_23, M1.pin_24, M1.pin_44, R1.Pin_0, R2.Pin_0, R3.Pin_0, R4.Pin_0, R5.Pin_0, R6.Pin_0, R7.Pin_0, R8.Pin_0, R9.Pin_0, R10.Pin_0, R11.Pin_1, R12.Pin_1, R13.Pin_1, R14.Pin_1, R15.Pin_1, R16.Pin_0, R17.Pin_0
  N20: LED1.cathode, R11.Pin_0
  N21: LED2.cathode, R12.Pin_0
  N22: LED3.cathode, R13.Pin_0
  N23: LED4.cathode, R14.Pin_0
  N24: LED5.cathode, R15.Pin_0
  N25: LED6.cathode, R16.Pin_1

custom parts:
  ESP32-S3-DevKitC-1: ESP32-S2-DevKitC-1 is an entry-level development board based on ESP32-S2-SOLO (on-board PCB antenna). It is based on the ESP32 microcontroller that boasts Wifi, Bluetooth, Ethernet and Low Power support all in a single chip. (vanepp) Feb 2022: converted to ESP32-S2-DevKitC-1. This module is 44pins long (2x22) and 11 pins width.
